# Fritzing sketch currentsource_mod (saved by Fritzing 0.9.2b)
circuit board: 4cm x 2cm
breadboards: 1

parts:
  I_out- = Header 1 [package=1x01_offset]
  I_out+ = Header 1 [package=1x01_offset]
  V_pwr+ = Header 1 [package=1x01_offset]
  GND_pwr = Header 1 [package=1x01_offset]
  I_set = Header 1 [package=1x01_offset]
  V_ctl = Header 1 [package=1x01_offset]
  GND_ctrl = Header 1 [package=1x01_offset]
  PWM = Header 1 [package=1x01_offset]
  NCHANpwr = Basic FET N-Channel [package="TO220 [THT]"]
  OPAMP1 = Dual Op-Amp [package=dip08]
  R3 = Resistor [tolerance=±5% resistance=100k package="1206 [SMD]"]
  Rpwm1 = Resistor [tolerance=±5% resistance=1k package="1206 [SMD]"]
  Rmosfet1 = Resistor [tolerance=±5% resistance=100 package="1206 [SMD]"]
  Rsense = Resistor [tolerance=±5% resistance=0.1 power=2W package="2010 [SMD]"]
  Rpwm2 = Resistor [tolerance=±5% resistance=100k power=2W package="1206 [SMD]"]
  Risetfilter = Resistor [tolerance=±5% resistance=100k package="1206 [SMD]"]
  Cisetfilter = Electrolytic Capacitor [capacitance=1µF package="0605 [SMD, electrolytic]"]
  NPNpwm = NPN-Transistor [package="SOT-23 [SMD]"]

nets:
  N1: I_out-.1, NCHANpwr.drain
  N2: I_out+.1, V_pwr+.1
  N3: GND_pwr.1, GND_ctrl.1, OPAMP1.A_V-, Rsense.Pin_1, Rpwm2.Pin_1, Cisetfilter.-, NPNpwm.2
  N4: I_set.1, Risetfilter.Pin_0
  N5: V_ctl.1, OPAMP1.A_V+
  N6: PWM.1, Rpwm1.Pin_0, Rpwm2.Pin_0
  N7: NCHANpwr.gate, Rmosfet1.Pin_1
  N8: NCHANpwr.source, OPAMP1.B_-IN, Rsense.Pin_0
  N9: OPAMP1.A_OUT, OPAMP1.A_-IN, R3.Pin_0
  N10: OPAMP1.A_+IN, Risetfilter.Pin_1, Cisetfilter.+
  N11: OPAMP1.B_+IN, R3.Pin_1, NPNpwm.1
  N12: OPAMP1.B_OUT, Rmosfet1.Pin_0
  N13: Rpwm1.Pin_1, NPNpwm.0
